// Logisim project Display7-12char-logic.circ as structural Verilog
module main (
  input  _0,
  input  _1,
  input  _2,
  input  _3,
  input  _4,
  input  _5,
  input  _6,
  input  _7,
  input  _8,
  input  _9,
  input  A,
  input  B
);

  wire cc_1_a, cc_1_b, cc_1_c, cc_1_d, cc_1_e, cc_1_f, cc_1_g, cc_1_pt;

  CC cc_1 (
    .B0(_0), .B1(_1), .B2(_2), .B3(_3), .B4(_4), .B5(_5), .B6(_6), .B7(_7), .B8(_8), .B9(_9), .Ba(A), .Bb(B),
    .A(cc_1_a), .B(cc_1_b), .C(cc_1_c), .D(cc_1_d), .E(cc_1_e), .F(cc_1_f), .G(cc_1_g), .PT(cc_1_pt));
  _7_Segment_Display u_7_segment_display_1 (
    .g(cc_1_g), .f(cc_1_f), .a(cc_1_a), .b(cc_1_b), .e(cc_1_e), .d(cc_1_d), .c(cc_1_c), .dp(cc_1_pt));
endmodule
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