// Logisim project NAND-circuit.circ as structural Verilog: 1 circuit, main circuit main
module main (
  input  in_1,
  input  in_2,
  input  in_3,
  input  in_4,
  input  in_5,
  input  in_6,
  output out_7,
  output out_8,
  output out_9
);

  wire transistor_3_out, transistor_6_out;

  Pull_Resistor #(.pull(1)) pull_resistor_1 (.node(out_7));
  Transistor #(.\type ("n")) transistor_1 (.in(1'b0), .out(out_7), .gate(in_4));
  LED led_1 (.in(out_7));
  Transistor #(.\type ("n")) transistor_2 (.in(1'b0), .out(out_7), .gate(in_5));
  Transistor transistor_3 (.in(1'b1), .out(transistor_3_out), .gate(in_2));
  Transistor transistor_4 (.in(transistor_3_out), .out(out_9), .gate(in_6));
  Pull_Resistor pull_resistor_2 (.node(out_9));
  LED led_2 (.in(out_9));
  Transistor #(.\type ("n")) transistor_5 (.in(1'b0), .out(out_8), .gate(in_1));
  Transistor transistor_6 (.in(1'b1), .out(transistor_6_out), .gate(in_1));
  Transistor transistor_7 (.in(transistor_6_out), .out(out_8), .gate(in_3));
  LED led_3 (.in(out_8));
  Transistor #(.\type ("n")) transistor_8 (.in(1'b0), .out(out_8), .gate(in_3));

  // Notes on the sheet:
  //   NAND
endmodule
