// Logisim project XNOR-circuit.circ as structural Verilog: 1 circuit, main circuit main
module main (
  input  in_1,
  input  in_2,
  input  in_3,
  input  in_4,
  input  in_5,
  input  in_6,
  output out_7,
  output out_8
);

  wire transistor_1_out, transistor_5_out, transistor_7_out, transistor_9_out, transistor_10_out,
       transistor_12_out;

  Transistor #(.\type ("n")) transistor_1 (.in(1'b0), .out(transistor_1_out), .gate(in_5));
  Pull_Resistor #(.pull(1)) pull_resistor_1 (.node(out_7));
  Transistor transistor_2 (.in(transistor_1_out), .out(out_7), .gate(in_5));
  Transistor #(.\type ("n")) transistor_3 (.in(1'b0), .out(transistor_1_out), .gate(in_6));
  LED led_1 (.in(out_7));
  Transistor transistor_4 (.in(transistor_1_out), .out(out_7), .gate(in_6));
  Transistor #(.\type ("n")) transistor_5 (.in(1'b1), .out(transistor_5_out), .gate(in_3));
  Transistor #(.\type ("n")) transistor_6 (.in(transistor_5_out), .out(out_8), .gate(in_4));
  Pull_Resistor pull_resistor_2 (.node(out_8));
  Transistor transistor_7 (.in(1'b1), .out(transistor_7_out), .gate(in_4));
  Transistor transistor_8 (.in(transistor_7_out), .out(out_8), .gate(in_3));
  LED led_2 (.in(out_8));
  Transistor transistor_9 (.in(1'b1), .out(transistor_9_out), .gate(in_2));
  Transistor transistor_10 (.in(transistor_9_out), .out(transistor_10_out), .gate(in_1));
  Transistor transistor_11 (.in(transistor_12_out), .out(transistor_10_out), .gate(in_2));
  Transistor #(.\type ("n")) transistor_12 (.in(1'b0), .out(transistor_12_out), .gate(in_2));
  Transistor #(.\type ("n")) transistor_13 (.in(1'b1), .out(transistor_9_out), .gate(in_1));
  Transistor #(.\type ("n")) transistor_14 (.in(transistor_9_out), .out(transistor_10_out), .gate(in_2));
  LED led_3 (.in(transistor_10_out));
  Transistor transistor_15 (.in(transistor_12_out), .out(transistor_10_out), .gate(in_1));
  Transistor #(.\type ("n")) transistor_16 (.in(1'b0), .out(transistor_12_out), .gate(in_1));

  // Notes on the sheet:
  //   XNOR
endmodule
